# Fritzing sketch ConexiónRC522 (saved by Fritzing 1.0.2b)

parts:
  Componente1 = RFID-RC522 [part_number=101218]
  Componente2 = Arduino Nano (Rev3.0)

nets:
  N1: Componente1.SDA, Componente2.D10
  N2: Componente1.SCK, Componente2.D13/SCK
  N3: Componente1.MOSI, Componente2.D11/MOSI
  N4: Componente1.MISO, Componente2.D12/MISO
  GND: Componente1.GND, Componente2.GND
  3.3V: Componente1.3.3V, Componente2.3V3
